# Fritzing sketch ESP32_6050_5883 (saved by Fritzing 0.9.6b)

parts:
  Part3 = InvenSense MPU6050
  MH-ET_Live_Minikit_for_ESP1 = MH-ET Live Minikit for ESP32
  Part4 = Triple Axis Magnetometer - HMC5883 Breakout

nets:
  VCC: Part3.VCC, MH-ET_Live_Minikit_for_ESP1.3.3V, Part4.VCC
  GND: Part3.GND, Part4.GND
  N1: Part3.SCL, MH-ET_Live_Minikit_for_ESP1.IO22, Part4.SCL
  N2: Part3.SDA, MH-ET_Live_Minikit_for_ESP1.IO21, Part4.SDA

notes:
  + 5V DC

custom parts:
  MH-ET Live Minikit for ESP32: MH-ET Live Minikit for ESP32 ( http://mh.nodebb.com/topic/8/mh-et-live-minikit-for-esp32/2/) PCB footprint is invalid.
